// Logisim project Circuit.circ as structural Verilog: 7 circuits, main circuit Fulladder
module Fulladder (
  input  A,
  input  B,
  input  Cin,
  output Sum,
  output Cout
);

  wire and_1_out, and_2_out, and_3_out, xor_1_out;

  xor xor_1 (xor_1_out, A, B);
  and and_1 (and_1_out, A, B);
  and and_2 (and_2_out, A, Cin);
  and and_3 (and_3_out, B, Cin);
  xor xor_2 (Sum, xor_1_out, Cin);
  or or_1 (Cout, and_1_out, and_2_out, and_3_out);
endmodule

module Ripple (
  input  B3,
  input  A3,
  input  B2,
  input  A2,
  input  B1,
  input  A1,
  input  Cin,
  input  B0,
  input  A0,
  output Cout,
  output Sum3,
  output Sum2,
  output Sum1,
  output Sum0
);

  wire fulladder_2_cout, fulladder_3_cout, fulladder_4_cout;

  Fulladder fulladder_1 (.A(A3), .B(B3), .Cin(fulladder_2_cout), .Sum(Sum3), .Cout(Cout));
  Fulladder fulladder_2 (.A(A2), .B(B2), .Cin(fulladder_3_cout), .Sum(Sum2), .Cout(fulladder_2_cout));
  Fulladder fulladder_3 (.A(A1), .B(B1), .Cin(fulladder_4_cout), .Sum(Sum1), .Cout(fulladder_3_cout));
  Fulladder fulladder_4 (.A(A0), .B(B0), .Cin(Cin), .Sum(Sum0), .Cout(fulladder_4_cout));
endmodule

module BCD1digit (
  input  B3,
  input  A3,
  input  B2,
  input  A2,
  input  B1,
  input  A1,
  input  B0,
  input  A0,
  input  Cin,
  input  _0,
  output Sum3,
  output Sum2,
  output Sum1,
  output Sum0,
  output Cout
);

  wire and_1_out, and_2_out, ripple_1_cout, ripple_1_sum0, ripple_1_sum1, ripple_1_sum2, ripple_1_sum3;

  or or_1 (Cout, ripple_1_cout, and_1_out, and_2_out);
  and and_1 (and_1_out, ripple_1_sum1, ripple_1_sum3);
  and and_2 (and_2_out, ripple_1_sum2, ripple_1_sum3);
  Ripple ripple_1 (
    .B3(B3), .A3(A3), .B2(B2), .A2(A2), .B1(B1), .A1(A1), .Cin(Cin), .B0(B0), .A0(A0), .Cout(ripple_1_cout),
    .Sum3(ripple_1_sum3), .Sum2(ripple_1_sum2), .Sum1(ripple_1_sum1), .Sum0(ripple_1_sum0));
  Ripple ripple_2 (
    .B3(_0), .A3(ripple_1_sum3), .B2(Cout), .A2(ripple_1_sum2), .B1(Cout), .A1(ripple_1_sum1), .Cin(_0),
    .B0(_0), .A0(ripple_1_sum0), .Sum3(Sum3), .Sum2(Sum2), .Sum1(Sum1), .Sum0(Sum0));  // open: Cout
endmodule

module BCD3_digit (
  input  B11,
  input  A11,
  input  B10,
  input  A10,
  input  B9,
  input  A9,
  input  B8,
  input  A8,
  input  B7,
  input  A7,
  input  B6,
  input  A6,
  input  B5,
  input  A5,
  input  B4,
  input  A4,
  input  B3,
  input  A3,
  input  B2,
  input  A2,
  input  B1,
  input  A1,
  input  B0,
  input  A0,
  input  Cin,
  input  _0,
  output Sum11,
  output Sum10,
  output Sum9,
  output Sum8,
  output Sum7,
  output Sum6,
  output Sum5,
  output Sum4,
  output Sum3,
  output Sum2,
  output Sum1,
  output Sum0,
  output Cout
);

  wire bcd1digit_2_cout, bcd1digit_3_cout;

  BCD1digit bcd1digit_1 (
    .Cin(bcd1digit_2_cout), ._0(_0), .B3(B11), .A3(A11), .B2(B10), .A2(A10), .B1(B9), .A1(A9), .B0(B8),
    .A0(A8), .Cout(Cout), .Sum3(Sum11), .Sum2(Sum10), .Sum1(Sum9), .Sum0(Sum8));
  BCD1digit bcd1digit_2 (
    .Cin(bcd1digit_3_cout), ._0(_0), .B3(B7), .A3(A7), .B2(B6), .A2(A6), .B1(B5), .A1(A5), .B0(B4), .A0(A4),
    .Cout(bcd1digit_2_cout), .Sum3(Sum7), .Sum2(Sum6), .Sum1(Sum5), .Sum0(Sum4));
  BCD1digit bcd1digit_3 (
    .Cin(Cin), ._0(_0), .B3(B3), .A3(A3), .B2(B2), .A2(A2), .B1(B1), .A1(A1), .B0(B0), .A0(A0),
    .Cout(bcd1digit_3_cout), .Sum3(Sum3), .Sum2(Sum2), .Sum1(Sum1), .Sum0(Sum0));
endmodule

module _4_bitCla (
  input  Cin,
  input  A0,
  input  B0,
  input  A1,
  input  B1,
  input  A2,
  input  B2,
  input  A3,
  input  B3,
  output Sum0,
  output Sum1,
  output Sum2,
  output Sum3,
  output Cout
);

  wire C1_out, C2_out, C3_out, G0_out, G1_out, G2_out, G3_out, P0_out, P1_out, P1G0_out, P1P0C0_out, p2_out,
       P2G1_out, P2P1G0_out, P2P1POC0_out, P3_out, P3G2_out, P3P2G1_out, P3P2P1G0_out, P3P2P1P0C0_out,
       POC0_out;

  and G0 (G0_out, A0, B0);
  xor P0 (P0_out, A0, B0);
  and G1 (G1_out, A1, B1);
  xor P1 (P1_out, A1, B1);
  and G2 (G2_out, A2, B2);
  xor p2 (p2_out, A2, B2);
  and G3 (G3_out, A3, B3);
  xor P3 (P3_out, A3, B3);
  and POC0 (POC0_out, P0_out, Cin);
  and P1P0C0 (P1P0C0_out, POC0_out, P1_out);
  and P1G0 (P1G0_out, P1_out, G0_out);
  and P2G1 (P2G1_out, G1_out, p2_out);
  and P2P1G0 (P2P1G0_out, P1G0_out, p2_out);
  and P2P1POC0 (P2P1POC0_out, p2_out, P1P0C0_out);
  and P3G2 (P3G2_out, P3_out, G2_out);
  and P3P2G1 (P3P2G1_out, P2G1_out, P3_out);
  and P3P2P1G0 (P3P2P1G0_out, P2P1G0_out, P3_out);
  and P3P2P1P0C0 (P3P2P1P0C0_out, P2P1POC0_out, P3_out);
  or C1 (C1_out, G0_out, POC0_out);
  or C2 (C2_out, G1_out, P1G0_out, P1P0C0_out);
  or C3 (C3_out, G2_out, P2G1_out, P2P1G0_out, P2P1POC0_out);
  xor u_Sum0 (Sum0, Cin, P0_out);
  xor u_Sum1 (Sum1, C1_out, P1_out);
  xor u_Sum2 (Sum2, C2_out, p2_out);
  xor u_Sum3 (Sum3, C3_out, P3_out);
  or C4_Cout (Cout, G3_out, P3G2_out, P3P2G1_out, P3P2P1G0_out, P3P2P1P0C0_out);
endmodule

module BCD1digitCla (
  input  B3,
  input  A3,
  input  B2,
  input  A2,
  input  B1,
  input  A1,
  input  B0,
  input  A0,
  input  Cin,
  input  _0,
  output Sum3,
  output Sum2,
  output Sum1,
  output Sum0,
  output Cout
);

  wire and_1_out, and_2_out, n4_bitcla_1_cout, n4_bitcla_1_sum0, n4_bitcla_1_sum1, n4_bitcla_1_sum2,
       n4_bitcla_1_sum3;

  or or_1 (Cout, n4_bitcla_1_cout, and_1_out, and_2_out);
  and and_1 (and_1_out, n4_bitcla_1_sum3, n4_bitcla_1_sum2);
  and and_2 (and_2_out, n4_bitcla_1_sum1, n4_bitcla_1_sum3);
  _4_bitCla u_4_bitcla_1 (
    .Cin(Cin), .Sum0(n4_bitcla_1_sum0), .A0(A0), .B0(B0), .A1(A1), .B1(B1), .Sum2(n4_bitcla_1_sum2), .A2(A2),
    .B2(B2), .A3(A3), .B3(B3), .Sum3(n4_bitcla_1_sum3), .Cout(n4_bitcla_1_cout), .Sum1(n4_bitcla_1_sum1));
  _4_bitCla u_4_bitcla_2 (
    .Cin(_0), .Sum0(Sum0), .A0(n4_bitcla_1_sum0), .B0(_0), .A1(n4_bitcla_1_sum1), .B1(Cout), .Sum2(Sum2),
    .A2(n4_bitcla_1_sum2), .B2(Cout), .A3(n4_bitcla_1_sum3), .B3(_0), .Sum3(Sum3), .Sum1(Sum1));  // open: Cout
endmodule

module _3digitBcdCla (
  input  B3,
  input  A11,
  input  B10,
  input  A10,
  input  B9,
  input  A9,
  input  B8,
  input  A8,
  input  B7,
  input  A7,
  input  B6,
  input  A6,
  input  B5,
  input  A5,
  input  B4,
  input  A4,
  input  B3_2,
  input  A3,
  input  B2,
  input  A2,
  input  B1,
  input  A1,
  input  B0,
  input  A0,
  input  Cin,
  input  _0,
  output Cout,
  output Sum10,
  output Sum8,
  output Sum7,
  output Sum6,
  output Sum2,
  output Sum3,
  output Sum9,
  output Sum5,
  output Sum4,
  output Sum3_2,
  output Sum1,
  output Sum0
);

  wire bcd1digitcla_2_cout, bcd1digitcla_3_cout;

  BCD1digitCla bcd1digitcla_1 (
    .Cin(bcd1digitcla_2_cout), ._0(_0), .B3(B3), .A3(A11), .B2(B10), .A2(A10), .B1(B9), .A1(A9), .B0(B8),
    .A0(A8), .Cout(Cout), .Sum3(Sum3), .Sum2(Sum10), .Sum1(Sum9), .Sum0(Sum8));
  BCD1digitCla bcd1digitcla_2 (
    .Cin(bcd1digitcla_3_cout), ._0(_0), .B3(B7), .A3(A7), .B2(B6), .A2(A6), .B1(B5), .A1(A5), .B0(B4),
    .A0(A4), .Cout(bcd1digitcla_2_cout), .Sum3(Sum7), .Sum2(Sum6), .Sum1(Sum5), .Sum0(Sum4));
  BCD1digitCla bcd1digitcla_3 (
    .Cin(Cin), ._0(_0), .B3(B3_2), .A3(A3), .B2(B2), .A2(A2), .B1(B1), .A1(A1), .B0(B0), .A0(A0),
    .Cout(bcd1digitcla_3_cout), .Sum3(Sum3_2), .Sum2(Sum2), .Sum1(Sum1), .Sum0(Sum0));
endmodule
